// Logisim project KeyboardInterface.circ as structural Verilog: 4 circuits, main circuit main
module main (
  input  PS2ClockIn,
  input  PS2DataIn
);

  wire initialresponse_1_ps2clockpulldown, initialresponse_1_ps2datapulldown, transistor_1_out,
       transistor_2_out;

  Pull_Resistor #(.pull(1)) pull_resistor_1 (.node(PS2ClockIn));
  Pull_Resistor #(.pull(1)) pull_resistor_2 (.node(PS2DataIn));
  Transistor #(.\type ("n")) transistor_1 (
    .in(PS2ClockIn), .out(transistor_1_out), .gate(initialresponse_1_ps2clockpulldown));
  Transistor #(.\type ("n")) transistor_2 (
    .in(PS2DataIn), .out(transistor_2_out), .gate(initialresponse_1_ps2datapulldown));
  InitialResponse initialresponse_1 (
    .PS2ClockIn(PS2ClockIn), .PS2DataIn(PS2DataIn), .PS2ClockPullDown(initialresponse_1_ps2clockpulldown),
    .PS2DataPullDown(initialresponse_1_ps2datapulldown));  // open: ResetRequired, PS2ClockOut, PS2DataOut
  // also tied to GND on the sheet: {transistor_1_out, transistor_2_out}
endmodule

module InitialResponse (
  input  PS2ClockIn,
  input  PS2DataIn,
  input  ResetRequired,
  output PS2ClockOut,
  output PS2DataOut,
  output PS2ClockPullDown,
  output PS2DataPullDown
);

  wire not_1_out;

  not not_1 (not_1_out, PS2ClockIn);
  and and_1 (PS2ClockPullDown, not_1_out, ResetRequired);

  assign PS2ClockOut = PS2ClockIn;
  assign PS2DataOut = PS2DataIn;
  assign PS2DataPullDown = 1'b0;

  // Notes on the sheet:
  //   Clock pulses low
  //   The only message we send is 0xFF, so don't want to ever pull data down
endmodule

module DecodeMessage (
  input  PS2ClockIn,
  input  PS2DataIn
);

  wire shift_register_1_p5, shift_register_1_p6, shift_register_1_p7, shift_register_1_p8,
       shift_register_1_p9, shift_register_1_p10, shift_register_1_p11, shift_register_1_p12;

  // Shift_Register #(.length(11), .trigger("falling")) shift_register_1: pin names not known; wires that end beside it: 1'b0, 1'b1, PS2ClockIn, PS2DataIn, shift_register_1_p5, shift_register_1_p6, shift_register_1_p7, shift_register_1_p8, shift_register_1_p9, shift_register_1_p10, shift_register_1_p11, shift_register_1_p12, shift_register_1_p5, shift_register_1_p6, shift_register_1_p7, shift_register_1_p8, shift_register_1_p9, shift_register_1_p10, shift_register_1_p11, shift_register_1_p12
endmodule

module DecodeMemory (
  input  Addr0,
  input  Addr1,
  input  Addr2,
  input  Addr3,
  input  Addr4,
  input  Addr5,
  input  Addr6,
  input  Addr7,
  output Data0,
  output Data1,
  output Data2,
  output Data3,
  output Data4,
  output Data5,
  output Data6,
  output Data7,
  output ReleaseKey,
  output ExtendedCode
);

  ROM DataMem (
    .addr({Addr7, Addr6, Addr5, Addr4, Addr3, Addr2, Addr1, Addr0}),
    .data({Data7, Data6, Data5, Data4, Data3, Data2, Data1, Data0}));
  Comparator comparator_1 (
    .a({Addr7, Addr6, Addr5, Addr4, Addr3, Addr2, Addr1, Addr0}), .b(8'hf0), .eq(ReleaseKey));  // open: gt, lt
  Comparator comparator_2 (
    .a({Addr7, Addr6, Addr5, Addr4, Addr3, Addr2, Addr1, Addr0}), .b(8'he0), .eq(ExtendedCode));  // open: gt, lt
endmodule
